// Logisim project alu.circ as structural Verilog: 1 circuit, main circuit main
module main (
  input  [7:0] in_1,
  input  [7:0] in_2,
  input  [7:0] in_3,
  input  [7:0] in_4
);

  wire comparator_1_lt;
  wire [7:0] adder_1_out, adder_2_out, multiplexer_1_out, multiplexer_2_out, not_1_out, subtractor_1_out,
       undriven;

  Adder adder_1 (.a(in_1), .b(undriven), .out(adder_1_out));  // open: cin, cout
  Subtractor subtractor_1 (.a(in_1), .b(undriven), .out(subtractor_1_out));  // open: bin, bout
  assign not_1_out = ~in_1;  // NOT_Gate not_1, 8 bits wide
  Comparator comparator_1 (.a(in_1), .b(in_3), .lt(comparator_1_lt));  // open: gt, eq
  Adder adder_2 (.a(not_1_out), .b(in_2), .out(adder_2_out));  // open: cin, cout
  Multiplexer #(.width(8)) multiplexer_1 (.in0(in_1), .in1(in_4), .out(multiplexer_1_out), .sel(comparator_1_lt));
  Multiplexer #(.width(8)) multiplexer_2 (
    .in0(in_1), .in1(adder_2_out), .out(multiplexer_2_out), .sel(comparator_1_lt));
  Multiplexer #(.select(2), .width(8)) multiplexer_3 (
    .in0(adder_1_out), .in1(subtractor_1_out), .in2(multiplexer_2_out), .in3(multiplexer_1_out));  // open: out, sel
endmodule
