// Logisim project proj3.circ as structural Verilog: 1 circuit, main circuit main
module main (
  input  [7:0] in_1,
  input  [7:0] in_2,
  input  _1,
  input  [7:0] in_4,
  input  [7:0] _00000000,
  input  [7:0] in_6,
  input  [2:0] _0,
  input  [2:0] _5,
  input  [1:0] _00,
  input  [2:0] _0_2,
  input  [2:0] _1_2,
  input  [1:0] _01,
  input  [2:0] _0_3,
  input  [2:0] _2,
  input  [1:0] _10,
  input  [2:0] _0_4,
  input  [2:0] _3,
  input  [1:0] _01_2,
  input  [1:0] _00_2,
  input  [2:0] _0_5,
  input  [1:0] _11,
  input  [2:0] _4,
  input  [1:0] _10_2,
  output [7:0] out_24,
  output [7:0] out_25,
  output [7:0] out_26,
  output [7:0] out_27,
  output [1:0] out_28
);

  wire button_1_out, clock_1_out, comparator_1_eq, comparator_2_eq, comparator_3_eq, comparator_4_eq,
       comparator_5_lt, comparator_6_eq, comparator_7_eq;
  wire [1:0] multiplexer_4_out;
  wire [2:0] multiplexer_1_out, multiplexer_2_out, multiplexer_3_out, multiplexer_8_out, multiplexer_9_out,
       or_1_out;
  wire [7:0] adder_1_out, adder_2_out, adder_3_out, adder_4_out, multiplexer_5_out, multiplexer_6_out,
       not_1_out, register_1_q, subtractor_1_out;

  Register register_1 (.D(adder_1_out), .en(_1), .clk(clock_1_out), .Q(register_1_q), .clr(button_1_out));
  Adder adder_1 (.a(in_1), .b(register_1_q), .out(adder_1_out), .cin(_1));  // open: cout
  Clock clock_1 (.out(clock_1_out));
  Button button_1 (.out(button_1_out));
  ROM rom_1 (.addr(register_1_q), .data(out_24));
  assign out_25 = {{2{out_24[5]}}, out_24[5:0]};  // Bit_Extender bit_extender_1
  Register register_2 (.D(out_27), .en(clock_1_out), .clk(clock_1_out), .Q(out_26));  // open: clr
  Comparator #(.mode("unsigned"), .width(2)) comparator_1 (
    .a(_00), .b(out_24[7:6]), .eq(comparator_1_eq));  // open: gt, lt
  Comparator #(.mode("unsigned"), .width(2)) comparator_2 (
    .a(_01), .b(out_24[7:6]), .eq(comparator_2_eq));  // open: gt, lt
  Comparator #(.mode("unsigned"), .width(2)) comparator_3 (
    .a(_10), .b(out_24[7:6]), .eq(comparator_3_eq));  // open: gt, lt
  Comparator #(.mode("unsigned"), .width(2)) comparator_4 (
    .a(_11), .b(out_24[7:6]), .eq(comparator_4_eq));  // open: gt, lt
  Adder adder_2 (.a(out_26), .b(out_25), .out(adder_2_out));  // open: cin, cout
  Subtractor subtractor_1 (.a(out_26), .b(out_25), .out(subtractor_1_out));  // open: bin, bout
  assign not_1_out = ~out_26;  // NOT_Gate not_1, 8 bits wide
  Comparator comparator_5 (.a(out_26), .b(in_4), .lt(comparator_5_lt));  // open: gt, eq
  Adder adder_3 (.a(out_25), .b(in_6), .out(adder_3_out));  // open: cin, cout
  Multiplexer #(.width(3)) multiplexer_1 (.in0(_0), .in1(_5), .out(multiplexer_1_out), .sel(comparator_1_eq));
  Multiplexer #(.width(3)) multiplexer_2 (.in0(_0_2), .in1(_1_2), .out(multiplexer_2_out), .sel(comparator_2_eq));
  Multiplexer #(.width(3)) multiplexer_3 (.in0(_0_3), .in1(_2), .out(multiplexer_3_out), .sel(comparator_3_eq));
  Adder adder_4 (.a(not_1_out), .b(in_2), .out(adder_4_out));  // open: cin, cout
  Multiplexer #(.width(2)) multiplexer_4 (
    .in0(_00_2), .in1(out_24[5:4]), .out(multiplexer_4_out), .sel(comparator_4_eq));
  Multiplexer #(.width(8)) multiplexer_5 (
    .in0(out_26), .in1(adder_4_out), .out(multiplexer_5_out), .sel(comparator_5_lt));
  Multiplexer #(.width(8)) multiplexer_6 (
    .in0(out_26), .in1(_00000000), .out(multiplexer_6_out), .sel(comparator_5_lt));
  Comparator #(.mode("unsigned"), .width(2)) comparator_6 (
    .a(_01_2), .b(multiplexer_4_out), .eq(comparator_6_eq));  // open: gt, lt
  Comparator #(.width(2)) comparator_7 (.a(_10_2), .b(multiplexer_4_out), .eq(comparator_7_eq));  // open: gt, lt
  Multiplexer #(.select(3), .width(8)) multiplexer_7 (
    .in1(adder_2_out), .in2(subtractor_1_out), .in3(multiplexer_5_out), .in4(multiplexer_6_out),
    .in5(adder_3_out), .out(out_27), .sel(or_1_out));  // open: in0, in6, in7
  Multiplexer #(.width(3)) multiplexer_8 (.in0(_0_4), .in1(_3), .out(multiplexer_8_out), .sel(comparator_6_eq));
  Multiplexer #(.width(3)) multiplexer_9 (.in0(_0_5), .in1(_4), .out(multiplexer_9_out), .sel(comparator_7_eq));
  assign or_1_out = multiplexer_1_out | multiplexer_2_out | multiplexer_3_out | multiplexer_8_out | multiplexer_9_out;  // OR_Gate or_1, 3 bits wide

  assign out_28 = out_24[7:6];

  // Notes on the sheet:
  //   contents of rom_1 (hex, n*v repeats v):
  //   20 ee 87 dd 60
  //   00000000
  //   00000001
  //   00000000
endmodule
