// Logisim project proj3.circ as structural Verilog: 1 circuit, main circuit main
module main (
  input  [7:0] in_1,
  input  _1,
  input  [7:0] in_3,
  input  [7:0] _00000000,
  input  [2:0] _0,
  input  [2:0] _5,
  input  [1:0] _00,
  input  [2:0] _0_2,
  input  [2:0] _1_2,
  input  [1:0] _01,
  input  [2:0] _0_3,
  input  [2:0] _2,
  input  [1:0] _10,
  input  [2:0] _0_4,
  input  [2:0] _3,
  input  [2:0] _4,
  input  _0_5,
  input  [1:0] _11,
  output [7:0] out_19,
  output [7:0] out_20,
  output [7:0] out_21,
  output [7:0] out_22,
  output [1:0] out_23,
  output [2:0] out_24,
  output [2:0] out_25
);

  wire button_1_out, clock_1_out, comparator_1_eq, comparator_2_eq, comparator_3_eq, comparator_4_eq,
       comparator_5_lt;
  wire [2:0] multiplexer_1_out, multiplexer_2_out, multiplexer_3_out, or_1_out;
  wire [7:0] adder_1_out, adder_2_out, multiplexer_5_out, multiplexer_6_out, negator_1_out, register_1_q,
       subtractor_1_out;

  Register register_1 (.D(adder_1_out), .en(_1), .clk(clock_1_out), .Q(register_1_q), .clr(button_1_out));
  Adder adder_1 (.a(in_1), .b(register_1_q), .out(adder_1_out));  // open: cin, cout
  Clock clock_1 (.out(clock_1_out));
  Button button_1 (.out(button_1_out));
  ROM rom_1 (.addr(register_1_q), .data(out_19));
  assign out_20 = {{2{out_19[5]}}, out_19[5:0]};  // Bit_Extender bit_extender_1
  Register register_2 (.D(out_22), .en(clock_1_out), .clk(clock_1_out), .Q(out_21));  // open: clr
  Comparator #(.mode("unsigned"), .width(2)) comparator_1 (
    .a(_00), .b(out_19[7:6]), .eq(comparator_1_eq));  // open: gt, lt
  Comparator #(.mode("unsigned"), .width(2)) comparator_2 (
    .a(_01), .b(out_19[7:6]), .eq(comparator_2_eq));  // open: gt, lt
  Comparator #(.mode("unsigned"), .width(2)) comparator_3 (
    .a(_10), .b(out_19[7:6]), .eq(comparator_3_eq));  // open: gt, lt
  Comparator #(.mode("unsigned"), .width(2)) comparator_4 (
    .a(_11), .b(out_19[7:6]), .eq(comparator_4_eq));  // open: gt, lt
  Adder adder_2 (.a(out_21), .b(out_20), .out(adder_2_out));  // open: cin, cout
  Subtractor subtractor_1 (.a(out_21), .b(out_20), .out(subtractor_1_out));  // open: bin, bout
  Negator negator_1 (.in(out_21), .out(negator_1_out));
  Comparator comparator_5 (.a(out_21), .b(in_3), .lt(comparator_5_lt));  // open: gt, eq
  Multiplexer #(.width(3)) multiplexer_1 (.in0(_0), .in1(_5), .out(multiplexer_1_out), .sel(comparator_1_eq));
  Multiplexer #(.width(3)) multiplexer_2 (.in0(_0_2), .in1(_1_2), .out(multiplexer_2_out), .sel(comparator_2_eq));
  Multiplexer #(.width(3)) multiplexer_3 (.in0(_0_3), .in1(_2), .out(multiplexer_3_out), .sel(comparator_3_eq));
  Multiplexer multiplexer_4 (.in0(_0_5), .in1(out_19[5]), .out(out_25[0]), .sel(comparator_4_eq));
  Multiplexer #(.width(8)) multiplexer_5 (
    .in0(out_21), .in1(negator_1_out), .out(multiplexer_5_out), .sel(comparator_5_lt));
  Multiplexer #(.width(8)) multiplexer_6 (
    .in0(out_21), .in1(_00000000), .out(multiplexer_6_out), .sel(comparator_5_lt));
  Multiplexer #(.select(3), .width(3)) multiplexer_7 (
    .in0(_0_4), .in1(_0_4), .in2(_0_4), .in3(_0_4), .in4(_0_4), .in5(_0_4), .in6(_3), .in7(_4), .out(out_24),
    .sel({out_19[7:6], out_25[0]}));
  Multiplexer #(.select(3), .width(8)) multiplexer_8 (
    .in1(adder_2_out), .in2(subtractor_1_out), .in3(multiplexer_5_out), .in4(multiplexer_6_out),
    .in5(out_20), .out(out_22), .sel(or_1_out));  // open: in0, in6, in7
  assign or_1_out = multiplexer_1_out | multiplexer_2_out | multiplexer_3_out | out_24;  // OR_Gate or_1, 3 bits wide

  assign out_23 = out_19[7:6];
  assign out_25[2:1] = out_19[7:6];

  // Notes on the sheet:
  //   00000001
  //   contents of rom_1 (hex, n*v repeats v):
  //   20 ee 87 dd 60
  //   00000000
endmodule
